// Logisim project 9.12_1.circ as structural Verilog: 8 circuits, main circuit main
module main (
  input  in_1
);

  wire ALUsrc, clk, ExtOp, IfBeq, MemWrite, RegDst, RegWrite, Zero;
  wire [1:0] ALUctr, MemtoReg;
  wire [4:0] A1_5, A2_5, A3_5, ins_address;
  wire [5:0] func;
  wire [10:6] imm_16;
  wire [31:0] ALUres_32, imm_32, MemRead_32, multiplexer_1_out, multiplexer_2_out, R17, R18, R19, R20, R21,
       RegRead_32a, RegRead_32b;
  wire [31:26] Instr_32;

  Multiplexer #(.width(32)) multiplexer_1 (.in0(RegRead_32b), .in1(imm_32), .out(multiplexer_1_out), .sel(ALUsrc));
  controller controller_1 (
    .o5(Instr_32[31]), .o4(Instr_32[30]), .o3(Instr_32[29]), .o2(Instr_32[28]), .o1(Instr_32[27]),
    .o0(Instr_32[26]), .f5(func[5]), .f4(func[4]), .f3(func[3]), .f2(func[2]), .f1(func[1]), .f0(func[0]),
    .IfBeq(IfBeq), .RegDst(RegDst), .MemtoReg1(MemtoReg[1]), .ALUctr1(ALUctr[0]), .ExtOp(ExtOp),
    .RegWrite(RegWrite), .MemWrite(MemWrite), .ALUsrc(ALUsrc), .ALUctr2(ALUctr[1]), .MemtoReg2(MemtoReg[0]));
  IFU ifu_1 (
    .Zero(Zero), .reset(in_1), .Instr_32({Instr_32, A1_5, A2_5, A3_5, imm_16, func}), .IfBeq(IfBeq),
    .clk(clk), .address(ins_address), .Instr({Instr_32, A1_5, A2_5, A3_5, imm_16, func}));
  EXT ext_1 (.ExtOp(ExtOp), .imm_16({A3_5, imm_16, func}), .Ext_imm(imm_32));
  Multiplexer #(.select(2), .width(32)) multiplexer_2 (
    .in0(ALUres_32), .in1(MemRead_32), .in2(imm_32), .out(multiplexer_2_out), .sel(MemtoReg));  // open: in3
  GPR gpr_1 (
    .RegWrite(RegWrite), .Wd_32(multiplexer_2_out), .RegDst(RegDst), .A1_5(A1_5), .A2_5(A2_5), .A3_5(A3_5),
    .clk(clk), .reset(in_1), .Rd1_32(RegRead_32a), .Rd2_32(RegRead_32b), .r17(R17), .r18(R18), .r19(R19),
    .r20(R20), .r21(R21));
  ALU alu_1 (
    .A32(RegRead_32a), .ALUctr(ALUctr), .clk(clk), .B32(multiplexer_1_out), .reset(in_1), .Zero(Zero),
    .ALUres_32(ALUres_32));
  DM dm_1 (
    .Wd_32(RegRead_32b), .MemtoReg(MemtoReg[0]), .MemWrite(MemWrite), .clk(clk), .reset(in_1),
    .address_32(ALUres_32), .Rd_32(MemRead_32));
  Clock clock_1 (.out(clk));
  // Probe on {Instr_32, A1_5, A2_5, A3_5, imm_16, func}
  // Probe on Instr_32
  // Probe on A1_5
  // Probe on A2_5
  // Probe on A3_5
  // Probe on func
  // Probe on {A3_5, imm_16, func}
  // Probe on R17
  // Probe on R18
  // Probe on R19
  // Probe on R20
  // Probe on R21
  // Probe on ins_address
  // Probe on IfBeq
  // Probe on Zero
  // Probe on RegDst
  // Probe on RegWrite
  // Probe on ALUsrc
  // Probe on MemtoReg
  // Probe on MemWrite
  // Probe on ALUctr
  // Probe on ExtOp

  // Other names for the same wires on the sheet: imm_16 (some bits) = {A3_5, func};
  //   Instr_32[25:0] = {A1_5, A2_5, A3_5, imm_16, func}; opcode[5:0] = Instr_32; reset = in_1

  // Notes on the sheet:
  //   lui
endmodule

module IFU (
  input  Zero,
  input  reset,
  input  [31:0] Instr_32,
  input  IfBeq,
  input  clk,
  output [4:0] address,
  output [31:0] Instr
);

  wire [31:0] adder_1_out, adder_2_out, bit_extender_1_out, multiplexer_1_out, multiplexer_2_out, PC_q,
       shifter_1_out;

  Adder #(.width(32)) adder_1 (.a({PC_q[31:7], address, PC_q[1:0]}), .b(32'h4), .out(adder_1_out));  // open: cin, cout
  assign bit_extender_1_out = {{16{Instr_32[15]}}, Instr_32[15:0]};  // Bit_Extender bit_extender_1
  Shifter #(.width(32)) shifter_1 (.in(bit_extender_1_out), .\dist (5'b00010), .out(shifter_1_out));
  Adder #(.width(32)) adder_2 (
    .a({PC_q[31:7], address, PC_q[1:0]}), .b(shifter_1_out), .out(adder_2_out));  // open: cin, cout
  Multiplexer #(.disabled("Z"), .width(32)) multiplexer_1 (
    .in0(adder_1_out), .in1(adder_2_out), .out(multiplexer_1_out), .sel(Zero));
  Multiplexer #(.disabled("Z"), .width(32)) multiplexer_2 (
    .in0(adder_1_out), .in1(multiplexer_1_out), .out(multiplexer_2_out), .sel(IfBeq));
  Register #(.width(32)) PC (
    .D(multiplexer_2_out), .Q({PC_q[31:7], address, PC_q[1:0]}), .clk(clk), .clr(reset));  // open: en
  ROM #(.addrWidth(5), .dataWidth(32)) IM (.addr(address), .data(Instr));

  // Other names for the same wires on the sheet: imm_16[15:0] = Instr_32[15:0]

  // Notes on the sheet:
  //   PC+4
  //   I型分支：PC相对寻址
  //   PC+imm<<2
  //   contents of IM (hex, n*v repeats v):
  //   3c11cccc 36723333 2329821 271a023 12540002 0 ae510004 8e550004
endmodule

module GPR (
  input  RegWrite,
  input  [31:0] Wd_32,
  input  RegDst,
  input  [4:0] A1_5,
  input  [4:0] A2_5,
  input  [4:0] A3_5,
  input  clk,
  input  reset,
  output [31:0] Rd1_32,
  output [31:0] Rd2_32,
  output [31:0] r17,
  output [31:0] r18,
  output [31:0] r19,
  output [31:0] r20,
  output [31:0] r21
);

  wire demultiplexer_1_out0, demultiplexer_1_out1, demultiplexer_1_out2, demultiplexer_1_out3,
       demultiplexer_1_out4, demultiplexer_1_out5, demultiplexer_1_out6, demultiplexer_1_out7,
       demultiplexer_1_out8, demultiplexer_1_out9, demultiplexer_1_out10, demultiplexer_1_out11,
       demultiplexer_1_out12, demultiplexer_1_out13, demultiplexer_1_out14, demultiplexer_1_out15,
       demultiplexer_1_out16, demultiplexer_1_out17, demultiplexer_1_out18, demultiplexer_1_out19,
       demultiplexer_1_out20, demultiplexer_1_out21, demultiplexer_1_out22, demultiplexer_1_out23,
       demultiplexer_1_out24, demultiplexer_1_out25, demultiplexer_1_out26, demultiplexer_1_out27,
       demultiplexer_1_out28, demultiplexer_1_out29, demultiplexer_1_out30, demultiplexer_1_out31;
  wire [4:0] multiplexer_1_out;
  wire [31:0] register_1_q, register_2_q, register_3_q, register_4_q, register_5_q, register_7_q,
       register_8_q, register_9_q, register_10_q, register_11_q, register_12_q, register_15_q, register_16_q,
       register_17_q, register_18_q, register_19_q, register_20_q, register_22_q, register_23_q,
       register_24_q, register_25_q, register_26_q, register_27_q, register_28_q, register_30_q,
       register_31_q, register_32_q;

  Multiplexer #(.width(5)) multiplexer_1 (.in0(A2_5), .in1(A3_5), .out(multiplexer_1_out), .sel(RegDst));
  Demultiplexer #(.select(5)) demultiplexer_1 (
    .out0(demultiplexer_1_out0), .out1(demultiplexer_1_out1), .out2(demultiplexer_1_out2),
    .out3(demultiplexer_1_out3), .out4(demultiplexer_1_out4), .out5(demultiplexer_1_out5),
    .out6(demultiplexer_1_out6), .out7(demultiplexer_1_out7), .out8(demultiplexer_1_out8),
    .out9(demultiplexer_1_out9), .out10(demultiplexer_1_out10), .out11(demultiplexer_1_out11),
    .out12(demultiplexer_1_out12), .out13(demultiplexer_1_out13), .out14(demultiplexer_1_out14),
    .out15(demultiplexer_1_out15), .out16(demultiplexer_1_out16), .out17(demultiplexer_1_out17),
    .out18(demultiplexer_1_out18), .out19(demultiplexer_1_out19), .out20(demultiplexer_1_out20),
    .out21(demultiplexer_1_out21), .out22(demultiplexer_1_out22), .out23(demultiplexer_1_out23),
    .out24(demultiplexer_1_out24), .out25(demultiplexer_1_out25), .out26(demultiplexer_1_out26),
    .out27(demultiplexer_1_out27), .out28(demultiplexer_1_out28), .out29(demultiplexer_1_out29),
    .out30(demultiplexer_1_out30), .out31(demultiplexer_1_out31), .in(RegWrite), .sel(multiplexer_1_out));
  Register #(.width(32)) register_1 (.D(Wd_32), .en(demultiplexer_1_out0), .Q(register_1_q), .clk(clk), .clr(reset));
  Register #(.width(32)) register_2 (.D(Wd_32), .en(demultiplexer_1_out4), .Q(register_2_q), .clk(clk), .clr(reset));
  Register #(.width(32)) register_3 (.D(Wd_32), .en(demultiplexer_1_out8), .Q(register_3_q), .clk(clk), .clr(reset));
  Register #(.width(32)) register_4 (.D(Wd_32), .en(demultiplexer_1_out12), .Q(register_4_q), .clk(clk), .clr(reset));
  Register #(.width(32)) register_5 (.D(Wd_32), .en(demultiplexer_1_out16), .Q(register_5_q), .clk(clk), .clr(reset));
  Register #(.width(32)) register_6 (.D(Wd_32), .en(demultiplexer_1_out20), .Q(r20), .clk(clk), .clr(reset));
  Register #(.width(32)) register_7 (.D(Wd_32), .en(demultiplexer_1_out24), .Q(register_7_q), .clk(clk), .clr(reset));
  Register #(.width(32)) register_8 (.D(Wd_32), .en(demultiplexer_1_out28), .Q(register_8_q), .clk(clk), .clr(reset));
  Register #(.width(32)) register_9 (.D(Wd_32), .en(demultiplexer_1_out1), .Q(register_9_q), .clk(clk), .clr(reset));
  Register #(.width(32)) register_10 (.D(Wd_32), .en(demultiplexer_1_out5), .Q(register_10_q), .clk(clk), .clr(reset));
  Register #(.width(32)) register_11 (.D(Wd_32), .en(demultiplexer_1_out9), .Q(register_11_q), .clk(clk), .clr(reset));
  Register #(.width(32)) register_12 (.D(Wd_32), .en(demultiplexer_1_out13), .Q(register_12_q), .clk(clk), .clr(reset));
  Register #(.width(32)) register_13 (.D(Wd_32), .en(demultiplexer_1_out17), .Q(r17), .clk(clk), .clr(reset));
  Register #(.width(32)) register_14 (.D(Wd_32), .en(demultiplexer_1_out21), .Q(r21), .clk(clk), .clr(reset));
  Register #(.width(32)) register_15 (.D(Wd_32), .en(demultiplexer_1_out25), .Q(register_15_q), .clk(clk), .clr(reset));
  Register #(.width(32)) register_16 (.D(Wd_32), .en(demultiplexer_1_out29), .Q(register_16_q), .clk(clk), .clr(reset));
  Register #(.width(32)) register_17 (.D(Wd_32), .en(demultiplexer_1_out2), .Q(register_17_q), .clk(clk), .clr(reset));
  Register #(.width(32)) register_18 (.D(Wd_32), .en(demultiplexer_1_out6), .Q(register_18_q), .clk(clk), .clr(reset));
  Register #(.width(32)) register_19 (.D(Wd_32), .en(demultiplexer_1_out10), .Q(register_19_q), .clk(clk), .clr(reset));
  Register #(.width(32)) register_20 (.D(Wd_32), .en(demultiplexer_1_out14), .Q(register_20_q), .clk(clk), .clr(reset));
  Register #(.width(32)) register_21 (.D(Wd_32), .en(demultiplexer_1_out18), .Q(r18), .clk(clk), .clr(reset));
  Register #(.width(32)) register_22 (.D(Wd_32), .en(demultiplexer_1_out22), .Q(register_22_q), .clk(clk), .clr(reset));
  Register #(.width(32)) register_23 (.D(Wd_32), .en(demultiplexer_1_out26), .Q(register_23_q), .clk(clk), .clr(reset));
  Register #(.width(32)) register_24 (.D(Wd_32), .en(demultiplexer_1_out30), .Q(register_24_q), .clk(clk), .clr(reset));
  Register #(.width(32)) register_25 (.D(Wd_32), .en(demultiplexer_1_out3), .Q(register_25_q), .clk(clk), .clr(reset));
  Register #(.width(32)) register_26 (.D(Wd_32), .en(demultiplexer_1_out7), .Q(register_26_q), .clk(clk), .clr(reset));
  Register #(.width(32)) register_27 (.D(Wd_32), .en(demultiplexer_1_out11), .Q(register_27_q), .clk(clk), .clr(reset));
  Register #(.width(32)) register_28 (.D(Wd_32), .en(demultiplexer_1_out15), .Q(register_28_q), .clk(clk), .clr(reset));
  Register #(.width(32)) register_29 (.D(Wd_32), .en(demultiplexer_1_out19), .Q(r19), .clk(clk), .clr(reset));
  Register #(.width(32)) register_30 (.D(Wd_32), .en(demultiplexer_1_out23), .Q(register_30_q), .clk(clk), .clr(reset));
  Register #(.width(32)) register_31 (.D(Wd_32), .en(demultiplexer_1_out27), .Q(register_31_q), .clk(clk), .clr(reset));
  Register #(.width(32)) register_32 (.D(Wd_32), .en(demultiplexer_1_out31), .Q(register_32_q), .clk(clk), .clr(reset));
  Multiplexer #(.select(5), .width(32)) multiplexer_2 (
    .in0(register_1_q), .in1(register_9_q), .in2(register_17_q), .in3(register_25_q), .in4(register_2_q),
    .in5(register_10_q), .in6(register_18_q), .in7(register_26_q), .in8(register_3_q), .in9(register_11_q),
    .in10(register_19_q), .in11(register_27_q), .in12(register_4_q), .in13(register_12_q),
    .in14(register_20_q), .in15(register_28_q), .in16(register_5_q), .in17(r17), .in18(r18), .in19(r19),
    .in20(r20), .in21(r21), .in22(register_22_q), .in23(register_30_q), .in24(register_7_q),
    .in25(register_15_q), .in26(register_23_q), .in27(register_31_q), .in28(register_8_q),
    .in29(register_16_q), .in30(register_24_q), .in31(register_32_q), .out(Rd1_32), .sel(A1_5));
  Multiplexer #(.select(5), .width(32)) multiplexer_3 (
    .in0(register_1_q), .in1(register_9_q), .in2(register_17_q), .in3(register_25_q), .in4(register_2_q),
    .in5(register_10_q), .in6(register_18_q), .in7(register_26_q), .in8(register_3_q), .in9(register_11_q),
    .in10(register_19_q), .in11(register_27_q), .in12(register_4_q), .in13(register_12_q),
    .in14(register_20_q), .in15(register_28_q), .in16(register_5_q), .in17(r17), .in18(r18), .in19(r19),
    .in20(r20), .in21(r21), .in22(register_22_q), .in23(register_30_q), .in24(register_7_q),
    .in25(register_15_q), .in26(register_23_q), .in27(register_31_q), .in28(register_8_q),
    .in29(register_16_q), .in30(register_24_q), .in31(register_32_q), .out(Rd2_32), .sel(A2_5));
endmodule

module ALU (
  input  [31:0] A32,
  input  [1:0] ALUctr,
  input  clk,
  input  [31:0] B32,
  input  reset,
  output Zero,
  output [31:0] ALUres_32
);

  wire [31:0] full_adder_1_sum, multiplexer_1_out, negator_1_out, or_1_out;

  full_adder full_adder_1 (
    .a0(A32[0]), .b0(multiplexer_1_out[0]), .a1(A32[1]), .b1(multiplexer_1_out[1]), .in_5(A32[2]),
    .in_6(multiplexer_1_out[2]), .a3(A32[3]), .in_8(multiplexer_1_out[3]), .in_9(A32[4]),
    .in_10(multiplexer_1_out[4]), .in_11(A32[5]), .b5(multiplexer_1_out[5]), .in_13(A32[6]),
    .in_14(multiplexer_1_out[6]), .in_15(A32[7]), .in_16(multiplexer_1_out[7]), .in_17(A32[8]),
    .in_18(multiplexer_1_out[8]), .in_19(A32[9]), .in_20(multiplexer_1_out[9]), .in_21(A32[10]),
    .in_22(multiplexer_1_out[10]), .in_23(A32[11]), .in_24(multiplexer_1_out[11]), .in_25(A32[12]),
    .in_26(multiplexer_1_out[12]), .in_27(A32[13]), .in_28(multiplexer_1_out[13]), .in_29(A32[14]),
    .in_30(multiplexer_1_out[14]), .in_31(A32[15]), .in_32(multiplexer_1_out[15]), .in_33(A32[16]),
    .in_34(multiplexer_1_out[16]), .in_35(A32[17]), .in_36(multiplexer_1_out[17]), .in_37(A32[18]),
    .in_38(multiplexer_1_out[18]), .in_39(A32[19]), .in_40(multiplexer_1_out[19]), .in_41(A32[20]),
    .in_42(multiplexer_1_out[20]), .in_43(A32[21]), .in_44(multiplexer_1_out[21]), .in_45(A32[22]),
    .in_46(multiplexer_1_out[22]), .in_47(A32[23]), .in_48(multiplexer_1_out[23]), .in_49(A32[24]),
    .in_50(multiplexer_1_out[24]), .in_51(A32[25]), .in_52(multiplexer_1_out[25]), .in_53(A32[26]),
    .in_54(multiplexer_1_out[26]), .in_55(A32[27]), .in_56(multiplexer_1_out[27]), .in_57(A32[28]),
    .in_58(multiplexer_1_out[28]), .in_59(A32[29]), .in_60(multiplexer_1_out[29]), .in_61(A32[30]),
    .in_62(multiplexer_1_out[30]), .in_63(A32[31]), .in_64(multiplexer_1_out[31]), .sum(full_adder_1_sum[0]),
    .a(full_adder_1_sum[1]), .b(full_adder_1_sum[2]), .c(full_adder_1_sum[3]), .out_69(full_adder_1_sum[4]),
    .out_70(full_adder_1_sum[5]), .out_71(full_adder_1_sum[6]), .g(full_adder_1_sum[7]),
    .out_73(full_adder_1_sum[8]), .out_74(full_adder_1_sum[9]), .out_75(full_adder_1_sum[10]),
    .k(full_adder_1_sum[11]), .out_77(full_adder_1_sum[12]), .out_78(full_adder_1_sum[13]),
    .out_79(full_adder_1_sum[14]), .out_80(full_adder_1_sum[15]), .out_81(full_adder_1_sum[16]),
    .out_82(full_adder_1_sum[17]), .out_83(full_adder_1_sum[18]), .out_84(full_adder_1_sum[19]),
    .out_85(full_adder_1_sum[20]), .out_86(full_adder_1_sum[21]), .out_87(full_adder_1_sum[22]),
    .out_88(full_adder_1_sum[23]), .out_89(full_adder_1_sum[24]), .out_90(full_adder_1_sum[25]),
    .out_91(full_adder_1_sum[26]), .out_92(full_adder_1_sum[27]), .out_93(full_adder_1_sum[28]),
    .out_94(full_adder_1_sum[29]), .out_95(full_adder_1_sum[30]), .out_96(full_adder_1_sum[31]));
  Negator #(.width(32)) negator_1 (.in(B32), .out(negator_1_out));
  Multiplexer #(.width(32)) multiplexer_1 (.in0(B32), .in1(negator_1_out), .out(multiplexer_1_out), .sel(ALUctr[0]));
  assign or_1_out = B32 | A32;  // OR_Gate or_1, 32 bits wide
  Multiplexer #(.width(32)) multiplexer_2 (.in0(or_1_out), .in1(full_adder_1_sum), .out(ALUres_32), .sel(ALUctr[1]));
  Comparator #(.width(32)) comparator_1 (.a(ALUres_32), .b({32{1'b0}}), .eq(Zero));  // open: gt, lt

  // Other names for the same wires on the sheet: C32[31:0] = ALUres_32

  // Notes on the sheet:
  //   10 add 11 sub 01 or
endmodule

module DM (
  input  [31:0] Wd_32,
  input  MemtoReg,
  input  MemWrite,
  input  clk,
  input  reset,
  input  [31:0] address_32,
  output [31:0] Rd_32
);

  RAM #(.addrWidth(5), .asyncread("true"), .clearpin("true"), .dataWidth(32)) ram_1 (
    .addr(address_32[6:2]), .we(MemWrite), .oe(MemtoReg), .clk(clk), .din(Wd_32), .dout(Rd_32), .clr(reset));

  // Other names for the same wires on the sheet: address_5[4:0] = address_32[6:2]
endmodule

module EXT (
  input  ExtOp,
  input  [15:0] imm_16,
  output [31:0] Ext_imm
);

  wire [31:0] bit_extender_1_out;

  assign bit_extender_1_out = {{16{1'b0}}, imm_16};  // Bit_Extender bit_extender_1
  Multiplexer #(.width(32)) multiplexer_1 (
    .in0(bit_extender_1_out), .in1({imm_16, {16{1'b0}}}), .out(Ext_imm), .sel(ExtOp));
endmodule

module full_adder (
  input  a0,
  input  b0,
  input  a1,
  input  b1,
  input  in_5,
  input  in_6,
  input  a3,
  input  in_8,
  input  in_9,
  input  in_10,
  input  in_11,
  input  b5,
  input  in_13,
  input  in_14,
  input  in_15,
  input  in_16,
  input  in_17,
  input  in_18,
  input  in_19,
  input  in_20,
  input  in_21,
  input  in_22,
  input  in_23,
  input  in_24,
  input  in_25,
  input  in_26,
  input  in_27,
  input  in_28,
  input  in_29,
  input  in_30,
  input  in_31,
  input  in_32,
  input  in_33,
  input  in_34,
  input  in_35,
  input  in_36,
  input  in_37,
  input  in_38,
  input  in_39,
  input  in_40,
  input  in_41,
  input  in_42,
  input  in_43,
  input  in_44,
  input  in_45,
  input  in_46,
  input  in_47,
  input  in_48,
  input  in_49,
  input  in_50,
  input  in_51,
  input  in_52,
  input  in_53,
  input  in_54,
  input  in_55,
  input  in_56,
  input  in_57,
  input  in_58,
  input  in_59,
  input  in_60,
  input  in_61,
  input  in_62,
  input  in_63,
  input  in_64,
  output sum,
  output a,
  output b,
  output c,
  output out_69,
  output out_70,
  output out_71,
  output g,
  output out_73,
  output out_74,
  output out_75,
  output k,
  output out_77,
  output out_78,
  output out_79,
  output out_80,
  output out_81,
  output out_82,
  output out_83,
  output out_84,
  output out_85,
  output out_86,
  output out_87,
  output out_88,
  output out_89,
  output out_90,
  output out_91,
  output out_92,
  output out_93,
  output out_94,
  output out_95,
  output out_96
);

  wire and_1_out, and_2_out, and_3_out, and_4_out, and_5_out, and_6_out, and_7_out, and_8_out, and_9_out,
       and_10_out, and_11_out, and_12_out, and_13_out, and_14_out, and_15_out, and_16_out, and_17_out,
       and_18_out, and_19_out, and_20_out, and_21_out, and_22_out, and_23_out, and_24_out, and_25_out,
       and_26_out, and_27_out, and_28_out, and_29_out, and_30_out, and_31_out, and_32_out, and_33_out,
       and_34_out, and_35_out, and_36_out, and_37_out, and_38_out, and_39_out, and_40_out, and_41_out,
       and_42_out, and_43_out, and_44_out, and_45_out, and_46_out, and_47_out, and_48_out, and_49_out,
       and_50_out, and_51_out, and_52_out, and_53_out, and_54_out, and_55_out, and_56_out, and_57_out,
       and_58_out, and_59_out, and_60_out, and_61_out, and_62_out, and_63_out, and_64_out, or_1_out,
       or_2_out, or_3_out, or_4_out, or_5_out, or_6_out, or_7_out, or_8_out, or_9_out, or_10_out, or_11_out,
       or_12_out, or_13_out, or_14_out, or_15_out, or_16_out, or_17_out, or_18_out, or_19_out, or_20_out,
       or_21_out, or_22_out, or_23_out, or_24_out, or_25_out, or_26_out, or_27_out, or_28_out, or_29_out,
       or_30_out, or_31_out, xor_1_out, xor_3_out, xor_5_out, xor_7_out, xor_9_out, xor_11_out, xor_13_out,
       xor_14_out, xor_17_out, xor_19_out, xor_21_out, xor_23_out, xor_25_out, xor_27_out, xor_29_out,
       xor_30_out, xor_33_out, xor_35_out, xor_37_out, xor_39_out, xor_41_out, xor_43_out, xor_45_out,
       xor_46_out, xor_49_out, xor_51_out, xor_53_out, xor_55_out, xor_57_out, xor_59_out, xor_61_out,
       xor_62_out;

  xor xor_1 (xor_1_out, a0, b0);
  and and_1 (and_1_out, b0, a0);
  xor xor_2 (sum, 1'b0, xor_1_out);
  and and_2 (and_2_out, 1'b0, xor_1_out);
  or or_1 (or_1_out, and_2_out, and_1_out);
  xor xor_3 (xor_3_out, a1, b1);
  and and_3 (and_3_out, b1, a1);
  xor xor_4 (a, or_1_out, xor_3_out);
  and and_4 (and_4_out, or_1_out, xor_3_out);
  or or_2 (or_2_out, and_4_out, and_3_out);
  xor xor_5 (xor_5_out, in_5, in_6);
  and and_5 (and_5_out, in_6, in_5);
  xor xor_6 (b, or_2_out, xor_5_out);
  and and_6 (and_6_out, or_2_out, xor_5_out);
  or or_3 (or_3_out, and_6_out, and_5_out);
  xor xor_7 (xor_7_out, a3, in_8);
  and and_7 (and_7_out, or_3_out, xor_7_out);
  and and_8 (and_8_out, in_8, a3);
  xor xor_8 (c, or_3_out, xor_7_out);
  or or_4 (or_4_out, and_7_out, and_8_out);
  xor xor_9 (xor_9_out, in_9, in_10);
  and and_9 (and_9_out, or_4_out, xor_9_out);
  and and_10 (and_10_out, in_10, in_9);
  xor xor_10 (out_69, or_4_out, xor_9_out);
  or or_5 (or_5_out, and_9_out, and_10_out);
  xor xor_11 (xor_11_out, in_11, b5);
  and and_11 (and_11_out, or_5_out, xor_11_out);
  and and_12 (and_12_out, b5, in_11);
  and and_13 (and_13_out, in_14, in_13);
  xor xor_12 (out_70, or_5_out, xor_11_out);
  or or_6 (or_6_out, and_11_out, and_12_out);
  xor xor_13 (xor_13_out, in_13, in_14);
  and and_14 (and_14_out, or_6_out, xor_13_out);
  or or_7 (or_7_out, and_14_out, and_13_out);
  xor xor_14 (xor_14_out, in_15, in_16);
  and and_15 (and_15_out, in_16, in_15);
  xor xor_15 (out_71, or_6_out, xor_13_out);
  xor xor_16 (g, or_7_out, xor_14_out);
  and and_16 (and_16_out, or_7_out, xor_14_out);
  or or_8 (or_8_out, and_16_out, and_15_out);
  xor xor_17 (xor_17_out, in_17, in_18);
  and and_17 (and_17_out, in_18, in_17);
  xor xor_18 (out_73, or_8_out, xor_17_out);
  and and_18 (and_18_out, or_8_out, xor_17_out);
  or or_9 (or_9_out, and_18_out, and_17_out);
  xor xor_19 (xor_19_out, in_19, in_20);
  and and_19 (and_19_out, in_20, in_19);
  xor xor_20 (out_74, or_9_out, xor_19_out);
  and and_20 (and_20_out, or_9_out, xor_19_out);
  or or_10 (or_10_out, and_20_out, and_19_out);
  xor xor_21 (xor_21_out, in_21, in_22);
  and and_21 (and_21_out, in_22, in_21);
  xor xor_22 (out_75, or_10_out, xor_21_out);
  and and_22 (and_22_out, or_10_out, xor_21_out);
  or or_11 (or_11_out, and_22_out, and_21_out);
  xor xor_23 (xor_23_out, in_23, in_24);
  and and_23 (and_23_out, or_11_out, xor_23_out);
  and and_24 (and_24_out, in_24, in_23);
  xor xor_24 (k, or_11_out, xor_23_out);
  or or_12 (or_12_out, and_23_out, and_24_out);
  xor xor_25 (xor_25_out, in_25, in_26);
  and and_25 (and_25_out, or_12_out, xor_25_out);
  and and_26 (and_26_out, in_26, in_25);
  xor xor_26 (out_77, or_12_out, xor_25_out);
  or or_13 (or_13_out, and_25_out, and_26_out);
  xor xor_27 (xor_27_out, in_27, in_28);
  and and_27 (and_27_out, or_13_out, xor_27_out);
  and and_28 (and_28_out, in_28, in_27);
  and and_29 (and_29_out, in_30, in_29);
  xor xor_28 (out_78, or_13_out, xor_27_out);
  or or_14 (or_14_out, and_27_out, and_28_out);
  xor xor_29 (xor_29_out, in_29, in_30);
  and and_30 (and_30_out, or_14_out, xor_29_out);
  or or_15 (or_15_out, and_30_out, and_29_out);
  xor xor_30 (xor_30_out, in_31, in_32);
  and and_31 (and_31_out, in_32, in_31);
  xor xor_31 (out_79, or_14_out, xor_29_out);
  xor xor_32 (out_80, or_15_out, xor_30_out);
  and and_32 (and_32_out, or_15_out, xor_30_out);
  or or_16 (or_16_out, and_32_out, and_31_out);
  xor xor_33 (xor_33_out, in_33, in_34);
  and and_33 (and_33_out, in_34, in_33);
  xor xor_34 (out_81, or_16_out, xor_33_out);
  and and_34 (and_34_out, or_16_out, xor_33_out);
  or or_17 (or_17_out, and_34_out, and_33_out);
  xor xor_35 (xor_35_out, in_35, in_36);
  and and_35 (and_35_out, in_36, in_35);
  xor xor_36 (out_82, or_17_out, xor_35_out);
  and and_36 (and_36_out, or_17_out, xor_35_out);
  or or_18 (or_18_out, and_36_out, and_35_out);
  xor xor_37 (xor_37_out, in_37, in_38);
  and and_37 (and_37_out, in_38, in_37);
  xor xor_38 (out_83, or_18_out, xor_37_out);
  and and_38 (and_38_out, or_18_out, xor_37_out);
  or or_19 (or_19_out, and_38_out, and_37_out);
  xor xor_39 (xor_39_out, in_39, in_40);
  and and_39 (and_39_out, or_19_out, xor_39_out);
  and and_40 (and_40_out, in_40, in_39);
  xor xor_40 (out_84, or_19_out, xor_39_out);
  or or_20 (or_20_out, and_39_out, and_40_out);
  xor xor_41 (xor_41_out, in_41, in_42);
  and and_41 (and_41_out, or_20_out, xor_41_out);
  and and_42 (and_42_out, in_42, in_41);
  xor xor_42 (out_85, or_20_out, xor_41_out);
  or or_21 (or_21_out, and_41_out, and_42_out);
  xor xor_43 (xor_43_out, in_43, in_44);
  and and_43 (and_43_out, or_21_out, xor_43_out);
  and and_44 (and_44_out, in_44, in_43);
  and and_45 (and_45_out, in_46, in_45);
  xor xor_44 (out_86, or_21_out, xor_43_out);
  or or_22 (or_22_out, and_43_out, and_44_out);
  xor xor_45 (xor_45_out, in_45, in_46);
  and and_46 (and_46_out, or_22_out, xor_45_out);
  or or_23 (or_23_out, and_46_out, and_45_out);
  xor xor_46 (xor_46_out, in_47, in_48);
  and and_47 (and_47_out, in_48, in_47);
  xor xor_47 (out_87, or_22_out, xor_45_out);
  xor xor_48 (out_88, or_23_out, xor_46_out);
  and and_48 (and_48_out, or_23_out, xor_46_out);
  or or_24 (or_24_out, and_48_out, and_47_out);
  xor xor_49 (xor_49_out, in_49, in_50);
  and and_49 (and_49_out, in_50, in_49);
  xor xor_50 (out_89, or_24_out, xor_49_out);
  and and_50 (and_50_out, or_24_out, xor_49_out);
  or or_25 (or_25_out, and_50_out, and_49_out);
  xor xor_51 (xor_51_out, in_51, in_52);
  and and_51 (and_51_out, in_52, in_51);
  xor xor_52 (out_90, or_25_out, xor_51_out);
  and and_52 (and_52_out, or_25_out, xor_51_out);
  or or_26 (or_26_out, and_52_out, and_51_out);
  xor xor_53 (xor_53_out, in_53, in_54);
  and and_53 (and_53_out, in_54, in_53);
  xor xor_54 (out_91, or_26_out, xor_53_out);
  and and_54 (and_54_out, or_26_out, xor_53_out);
  or or_27 (or_27_out, and_54_out, and_53_out);
  xor xor_55 (xor_55_out, in_55, in_56);
  and and_55 (and_55_out, or_27_out, xor_55_out);
  and and_56 (and_56_out, in_56, in_55);
  xor xor_56 (out_92, or_27_out, xor_55_out);
  or or_28 (or_28_out, and_55_out, and_56_out);
  xor xor_57 (xor_57_out, in_57, in_58);
  and and_57 (and_57_out, or_28_out, xor_57_out);
  and and_58 (and_58_out, in_58, in_57);
  xor xor_58 (out_93, or_28_out, xor_57_out);
  or or_29 (or_29_out, and_57_out, and_58_out);
  xor xor_59 (xor_59_out, in_59, in_60);
  and and_59 (and_59_out, or_29_out, xor_59_out);
  and and_60 (and_60_out, in_60, in_59);
  and and_61 (and_61_out, in_62, in_61);
  xor xor_60 (out_94, or_29_out, xor_59_out);
  or or_30 (or_30_out, and_59_out, and_60_out);
  xor xor_61 (xor_61_out, in_61, in_62);
  and and_62 (and_62_out, or_30_out, xor_61_out);
  or or_31 (or_31_out, and_62_out, and_61_out);
  xor xor_62 (xor_62_out, in_63, in_64);
  and and_63 (and_63_out, in_64, in_63);
  xor xor_63 (out_95, or_30_out, xor_61_out);
  xor xor_64 (out_96, or_31_out, xor_62_out);
  and and_64 (and_64_out, or_31_out, xor_62_out);
  // OR_Gate or_32 has open pins: in0=and_64_out, in1=and_63_out, out=open
endmodule

module controller (
  input  o5,
  input  o4,
  input  o3,
  input  o2,
  input  o1,
  input  o0,
  input  f5,
  input  f4,
  input  f3,
  input  f2,
  input  f1,
  input  f0,
  output IfBeq,
  output RegDst,
  output MemtoReg1,
  output ALUctr1,
  output ExtOp,
  output RegWrite,
  output MemWrite,
  output ALUsrc,
  output ALUctr2,
  output MemtoReg2
);

  wire addu_out, beq_out, lui_out, lw_out, not_1_out, not_2_out, not_3_out, not_4_out, not_5_out, not_6_out,
       not_7_out, not_8_out, not_9_out, not_10_out, not_11_out, not_12_out, ori_out, subu_out, sw_out;

  not not_1 (not_1_out, o5);
  not not_2 (not_2_out, o4);
  not not_3 (not_3_out, o3);
  not not_4 (not_4_out, o2);
  not not_5 (not_5_out, o1);
  not not_6 (not_6_out, o0);
  not not_7 (not_7_out, f5);
  not not_8 (not_8_out, f4);
  not not_9 (not_9_out, f3);
  not not_10 (not_10_out, f2);
  not not_11 (not_11_out, f1);
  not not_12 (not_12_out, f0);
  and addu (addu_out, not_1_out, not_2_out, not_3_out, not_4_out, not_5_out, not_6_out, f5, not_8_out, not_9_out, not_10_out, not_11_out, f0);
  and subu (subu_out, not_1_out, not_2_out, not_3_out, not_4_out, not_5_out, not_6_out, f5, not_8_out, not_9_out, not_10_out, f1, f0);
  and ori (ori_out, not_1_out, not_2_out, o3, o2, not_5_out, o0);
  and beq (beq_out, not_1_out, not_2_out, not_3_out, o2, not_5_out, not_6_out);
  and lw (lw_out, o5, not_2_out, not_3_out, not_4_out, o1, o0);
  and sw (sw_out, o5, not_2_out, o3, not_4_out, o1, o0);
  and lui (lui_out, not_1_out, not_2_out, o3, o2, o1, o0);
  buf or_1 (IfBeq, beq_out);  // OR_Gate
  or or_2 (RegWrite, addu_out, subu_out, ori_out, lw_out, lui_out);
  or or_3 (RegDst, addu_out, subu_out);  // OR_Gate
  buf or_4 (MemWrite, sw_out);  // OR_Gate
  buf or_5 (MemtoReg1, lui_out);  // OR_Gate
  or or_6 (ALUsrc, ori_out, lw_out, sw_out);  // OR_Gate
  or or_7 (ALUctr1, addu_out, subu_out, beq_out, lw_out, sw_out);
  or or_8 (ALUctr2, subu_out, ori_out, beq_out);
  buf or_9 (ExtOp, lui_out);  // OR_Gate
  buf or_10 (MemtoReg2, lw_out);  // OR_Gate
endmodule
